# Fritzing sketch xmas-pixels (saved by Fritzing 0.9.2b)
breadboards: 1

parts:
  Part1 = Arduino Uno (Rev3)
  neopixel1 = Neopixel Ring 12
  R1 = Resistor [tolerance=±5% resistance=470 package="2010 [SMD]"]
  S1 = Pushbutton [package="[THT]"]

nets:
  GND: Part1.GND, neopixel1.GND, S1.Pin_1, S1.Pin_2
  N1: Part1.D2, S1.Pin_3, S1.Pin_4
  N2: Part1.D6_PWM, R1.Pin_0
  5V: Part1.5V, neopixel1.VCC
  N3: neopixel1.IN, R1.Pin_1

custom parts:
  Neopixel Ring 12: Neopixel Ring x12
